// Logisim project Milestone 2 - Copy.circ as structural Verilog: 3 circuits, main circuit main
module main (
  input  in_1,
  input  in_2
);

  wire clock_1_out, piece_1_ac_ld, piece_1_ar_ld, piece_1_dr_ld, piece_1_ir_ld, piece_1_mem_read,
       piece_1_mem_write, piece_1_pc_inc, piece_1_pc_ld;
  wire [1:0] piece_1_a0;
  wire [2:0] piece_1_s0;
  wire [5:0] AR_q, bit_extender_1_out, bit_extender_2_out, PC_q;
  wire [15:0] AC_q, adder_1_out, and_1_out, bit_extender_3_out, bit_extender_4_out, DR_q, IR_q,
       multiplexer_1_out, multiplexer_2_out, not_1_out, or_1_out, ram_1_data, subtractor_1_out, TR_q,
       xor_1_out;

  Clock clock_1 (.out(clock_1_out));
  Register #(.width(16)) DR (.D(multiplexer_2_out), .en(piece_1_dr_ld), .Q(DR_q), .clk(clock_1_out));  // open: clr
  Register #(.width(16)) TR (.D(multiplexer_2_out), .en(in_1), .Q(TR_q), .clk(clock_1_out));  // open: clr
  Bit_Extender #(.in_width(16), .out_width(6)) bit_extender_1 (.in(multiplexer_2_out), .out(bit_extender_1_out));
  Bit_Extender #(.in_width(16), .out_width(6)) bit_extender_2 (.in(multiplexer_2_out), .out(bit_extender_2_out));
  Register #(.width(16)) IR (.D(multiplexer_2_out), .en(piece_1_ir_ld), .Q(IR_q), .clk(clock_1_out));  // open: clr
  Adder #(.width(16)) adder_1 (.a(DR_q), .b(AC_q), .out(adder_1_out));  // open: cin, cout
  Subtractor #(.width(16)) subtractor_1 (.a(AC_q), .b(DR_q), .out(subtractor_1_out));  // open: bin, bout
  assign and_1_out = DR_q & AC_q;  // AND_Gate and_1, 16 bits wide
  assign or_1_out = DR_q | AC_q;  // OR_Gate or_1, 16 bits wide
  assign xor_1_out = DR_q ^ AC_q;  // XOR_Gate xor_1, 16 bits wide
  assign not_1_out = ~AC_q;  // NOT_Gate not_1, 16 bits wide
  Register #(.width(6)) AR (.D(bit_extender_1_out), .en(piece_1_ar_ld), .Q(AR_q), .clk(clock_1_out));  // open: clr
  Counter #(.width(6), .max('h3f)) PC (
    .load(piece_1_pc_ld), .D(bit_extender_2_out), .count(piece_1_pc_inc), .Q(PC_q), .clk(clock_1_out));  // open: carry, clr
  assign bit_extender_3_out = {{10{1'b0}}, AR_q};  // Bit_Extender bit_extender_3
  assign bit_extender_4_out = {{10{1'b0}}, PC_q};  // Bit_Extender bit_extender_4
  Multiplexer #(.select(3), .width(16), .enable("false")) multiplexer_1 (
    .in0(adder_1_out), .in1(subtractor_1_out), .in2(DR_q), .in3(and_1_out), .in4(or_1_out), .in5(xor_1_out),
    .in6(not_1_out), .out(multiplexer_1_out), .sel({in_2, piece_1_a0}));  // open: in7
  RAM #(.addrWidth(6), .dataWidth(16), .bus("separate")) ram_1 (
    .addr(AR_q), .din(multiplexer_2_out), .data(ram_1_data), .str(piece_1_mem_write), .clk(clock_1_out),
    .ld(piece_1_mem_read));  // open: sel, clr
  Register #(.width(16)) AC (.D(multiplexer_1_out), .en(piece_1_ac_ld), .Q(AC_q), .clk(clock_1_out));  // open: clr
  piece piece_1 (
    .IR(IR_q), .clk(clock_1_out), .AC(AC_q), .A0(piece_1_a0[0]), .A1(piece_1_a0[1]), .DR_LD(piece_1_dr_ld),
    .AC_LD(piece_1_ac_ld), .Mem_Read(piece_1_mem_read), .Mem_Write(piece_1_mem_write), .PC_LD(piece_1_pc_ld),
    .IR_LD(piece_1_ir_ld), .PC_INC(piece_1_pc_inc), .AR_LD(piece_1_ar_ld), .S0(piece_1_s0[0]),
    .S1(piece_1_s0[1]), .S2(piece_1_s0[2]));
  Multiplexer #(.select(3), .width(16), .enable("false")) multiplexer_2 (
    .in0(AC_q), .in1(DR_q), .in2(TR_q), .in3(bit_extender_3_out), .in4(ram_1_data), .in5(bit_extender_4_out),
    .in6(IR_q), .out(multiplexer_2_out), .sel(piece_1_s0));  // open: in7
endmodule

module piece (
  input  [15:0] IR,
  input  clk,
  input  [15:0] AC,
  output A0,
  output A1,
  output DR_LD,
  output AC_LD,
  output Mem_Read,
  output Mem_Write,
  output PC_LD,
  output IR_LD,
  output PC_INC,
  output AR_LD,
  output S0,
  output S1,
  output S2
);

  wire and_1_out, and_2_out, d_ff_1_q, decoder_1_out0, decoder_1_out1, decoder_1_out2, decoder_1_out3,
       decoder_1_out4, decoder_1_out5, decoder_1_out6, decoder_1_out7, decoder_2_out0, decoder_2_out1,
       decoder_2_out2, decoder_2_out3, decoder_2_out4, decoder_2_out5, or_1_out, or_2_out, or_3_out;
  wire [3:0] SC_q;

  D_Flip_Flop d_ff_1 (.clk(clk), .D(or_3_out), .Q(d_ff_1_q));  // open: Qn, preset, en, reset
  Counter #(.width(4), .max('hf)) SC (.Q(SC_q), .clk(clk), .clr(d_ff_1_q));  // open: load, D, count, carry
  Decoder #(.select(3)) decoder_1 (
    .out0(decoder_1_out0), .out1(decoder_1_out1), .out2(decoder_1_out2), .out3(decoder_1_out3),
    .out4(decoder_1_out4), .out5(decoder_1_out5), .out6(decoder_1_out6), .out7(decoder_1_out7),
    .sel(IR[14:12]), .en(1'b1));
  or or_1 (or_1_out, decoder_1_out0, decoder_1_out1, decoder_1_out2);
  Decoder #(.select(4)) decoder_2 (
    .out0(decoder_2_out0), .out1(decoder_2_out1), .out2(decoder_2_out2), .out3(decoder_2_out3),
    .out4(decoder_2_out4), .out5(decoder_2_out5), .sel(SC_q));  // open: out6, out7, out8, out9, out10, out11, out12, out13, out14, out15, en
  and and_1 (and_1_out, decoder_2_out5, or_1_out);
  or or_2 (or_2_out, decoder_1_out4, decoder_1_out3);
  or or_3 (or_3_out, and_1_out, and_2_out);
  and and_2 (and_2_out, or_2_out, decoder_2_out4);
  intr intr_1 (
    .AR(IR[5:0]), .D0(decoder_1_out0), .D1(decoder_1_out1), .D2(decoder_1_out2), .D3(decoder_1_out3),
    .D4(decoder_1_out4), .D5(decoder_1_out5), .D6(decoder_1_out6), .D7(decoder_1_out7), .T0(decoder_2_out0),
    .T1(decoder_2_out1), .T2(decoder_2_out2), .I(IR[15]), .T3(decoder_2_out3), .T4(decoder_2_out4),
    .T5(decoder_2_out5), .AC(AC), .A0(A0), .A1(A1), .DR_LD(DR_LD), .AC_LD(AC_LD), .Mem_Read(Mem_Read),
    .Mem_Write(Mem_Write), .PC_LD(PC_LD), .IR_LD(IR_LD), .PC_INC(PC_INC), .AR_LD(AR_LD), .S0(S0), .S1(S1),
    .S2(S2));
endmodule

module intr (
  input  [5:0] AR,
  input  D0,
  input  D1,
  input  D2,
  input  D3,
  input  D4,
  input  D5,
  input  D6,
  input  D7,
  input  T0,
  input  T1,
  input  T2,
  input  I,
  input  T3,
  input  T4,
  input  T5,
  input  [15:0] AC,
  output A0,
  output A1,
  output DR_LD,
  output AC_LD,
  output Mem_Read,
  output Mem_Write,
  output PC_LD,
  output IR_LD,
  output PC_INC,
  output AR_LD,
  output S0,
  output S1,
  output S2
);

  wire and_6_out, not_1_out, or_1_out, or_5_out;

  or or_1 (or_1_out, D0, D1, D2, D5);
  and and_1 (Mem_Write, D3, T4);
  and and_2 (PC_LD, T4, D4);
  or or_2 (AR_LD, T0, T2);
  // AND_Gate and_3 has open pins: in0=I, in1=T3, out=open
  not not_1 (not_1_out, or_5_out);
  and and_4 (DR_LD, or_1_out, T4);
  or or_3 (S1, PC_LD, T2);
  or or_4 (Mem_Read, DR_LD, T1);
  or or_5 (or_5_out, AC[0], AC[1], AC[2], AC[3], AC[4], AC[5], AC[6], AC[7], AC[8], AC[9], AC[10], AC[11], AC[12], AC[13], AC[14], AC[15]);
  or or_6 (A0, D0, D5);
  and and_5 (AC_LD, or_1_out, T5);
  or or_7 (S2, T2, T0, T1, DR_LD);
  or or_8 (A1, D0, D2);
  or or_9 (S0, PC_LD, T0);
  or or_10 (PC_INC, T1, and_6_out);
  and and_6 (and_6_out, T3, D7, not_1_out, AR[2]);

  assign IR_LD = T1;
endmodule
